// Logisim project arquitetura.circ as structural Verilog: 1 circuit, main circuit main
module main (
  input  [7:0] matriz00,
  input  [7:0] matriz01,
  input  [7:0] matriz02,
  input  [7:0] matriz10,
  input  [7:0] matriz11,
  input  [7:0] matriz12,
  input  [7:0] matriz20,
  input  [7:0] matriz21,
  input  [7:0] matriz22,
  input  in_10,
  output [7:0] out_11
);

  wire [7:0] adder_1_out, adder_2_out, adder_3_out, adder_4_out, adder_5_out, adder_6_out, negator_1_out,
       negator_2_out, shifter_1_out, shifter_2_out;

  Adder adder_1 (.a(matriz00), .b(matriz02), .out(adder_1_out));  // open: cin, cout
  Shifter shifter_1 (.in(matriz01), .\dist (3'b001), .out(shifter_1_out));
  Negator negator_1 (.in(matriz20), .out(negator_1_out));
  Negator negator_2 (.in(matriz22), .out(negator_2_out));
  Shifter shifter_2 (.in(matriz21), .\dist (3'b001), .out(shifter_2_out));
  Adder adder_2 (.a(negator_1_out), .b(negator_2_out), .out(adder_2_out));  // open: cin, cout
  Adder adder_3 (.b(shifter_2_out), .out(adder_3_out));  // open: a, cin, cout
  Adder adder_4 (.a(adder_1_out), .b(shifter_1_out), .out(adder_4_out));  // open: cin, cout
  Adder adder_5 (.a(adder_2_out), .b(adder_3_out), .out(adder_5_out));  // open: cin, cout
  Adder adder_6 (.a(adder_4_out), .b(adder_5_out), .out(adder_6_out));  // open: cin, cout
  Register register_1 (.D(adder_6_out), .Q(out_11), .clk(in_10));  // open: en, clr
endmodule
